# Fritzing sketch Irrigatore (saved by Fritzing 0.9.4)
circuit board: 16.2748cm x 8.36545cm

parts:
  Componente1 = Arduino Nano (Rev3.0)
  Componente2 = Real Time Clock Module - DS1307 RTC Breakout Board
  LCD1 = LCD screen
  8_Channel_Relay1 = 8 Channel Power Relay
  LCM1602_IIC1 = LCM1602 IIC [part_number="LCM1602 IIC" chip_label="LCM1602 IIC" package="DIP (Dual Inline) [THT]"]
  Componente3 = 4x4 Keypad [part_number=101207]
  Componente4 = MCP23017 IO Expander
  DHT1 = DHT11 Humitidy and Temperature Sensor
  U1 = TRANSFORMER VB 1,5/1/9 [part_number="VB 1,5/1/9" package=transformer]
  U2 = TRANSFORMER VB 1,5/1/9 [part_number="VB 1,5/1/9" package=transformer]
  JP1 = RCA [package=rca_lock]
  JP2 = RCA [package=rca_lock]
  JP3 = RCA [package=rca_lock]
  JP4 = RCA [package=rca_lock]
  JP5 = RCA [package=rca_lock]
  JP6 = RCA [package=rca_lock]
  JP7 = RCA [package=rca_lock]
  JP8 = RCA [package=rca_lock]

nets:
  GND: Componente1.GND, Componente1.RESET, Componente2.GND, U1.4
  N1: Componente1.D2, Componente3.8
  N2: Componente1.D3, Componente3.7
  N3: Componente1.D4, Componente3.6
  N4: Componente1.D5, Componente3.5
  N5: Componente1.D6, Componente3.4
  N6: Componente1.D7, Componente3.3
  N7: Componente1.D8, Componente3.2
  N8: Componente1.D9, Componente3.1
  N9: Componente1.D10, DHT1.DATA
  N10: Componente1.VIN, U1.3
  5V: Componente1.5V, Componente1.A7, Componente2.5V
  N11: Componente1.A5, Componente2.SCL
  N12: Componente1.A4, Componente1.A3, Componente2.SDA
  VSS: LCD1.VSS, LCM1602_IIC1.VSS
  VDD: LCD1.VDD, LCM1602_IIC1.VDD
  N13: LCD1.V0, LCM1602_IIC1.V0
  N14: LCD1.RS, LCM1602_IIC1.RS
  N15: LCD1.R/W, LCM1602_IIC1.RW
  N16: LCD1.E, LCM1602_IIC1.E
  N17: LCD1.DB0, LCM1602_IIC1.D0
  N18: LCD1.DB1, LCM1602_IIC1.D1
  N19: LCD1.DB2, LCM1602_IIC1.D2
  N20: LCD1.DB3, LCM1602_IIC1.D3
  N21: LCD1.DB4, LCM1602_IIC1.D4
  N22: LCD1.DB5, LCM1602_IIC1.D5
  N23: LCD1.DB6, LCM1602_IIC1.D6
  N24: LCD1.DB7, LCM1602_IIC1.D7
  N25: LCD1.LED+, LCM1602_IIC1.A
  N26: LCD1.LED-, LCM1602_IIC1.K
  N27: 8_Channel_Relay1.IN1, Componente4.IO0
  N28: 8_Channel_Relay1.IN2, Componente4.IO1
  N29: 8_Channel_Relay1.IN3, Componente4.IO2
  N30: 8_Channel_Relay1.IN4, Componente4.IO3
  N31: 8_Channel_Relay1.IN5, Componente4.IO4
  N32: 8_Channel_Relay1.IN6, Componente4.IO5
  N33: 8_Channel_Relay1.IN7, Componente4.IO6
  N34: 8_Channel_Relay1.IN8, Componente4.IO7
  N35: 8_Channel_Relay1.NO#23, JP1.SHELL
  N36: 8_Channel_Relay1.NO#26, JP2.SHELL
  N37: 8_Channel_Relay1.NO#29, JP3.SHELL
  N38: 8_Channel_Relay1.NO#32, JP4.SHELL
  N39: 8_Channel_Relay1.NO#35, JP5.SHELL
  N40: 8_Channel_Relay1.NO#38, JP6.SHELL
  N41: 8_Channel_Relay1.NO#41, JP7.SHELL
  N42: 8_Channel_Relay1.COM#43, U2.3
  N43: 8_Channel_Relay1.NO#44, JP8.SHELL

notes:
  Convertitore I2C->8 bit I/O
  Display LCD 2x16 con schedina I2C
  Modulo RTC I2C
  Sensore DHT11 (facoltativo)
  Alimentatore 220->5V 1A
  Input 220V ~
  Alimentatore 220->12V 1A
  Attenzione che ogni valvola a solenoide assorbe 500mA, quindi .... non accenderne troppe insieme!
  8 prese a pannello (o 4 prese a 4 contatti) per pilotare le valvole a solenoide per l'irrigazione
  Arduino Nano

custom parts:
  8 Channel Power Relay: An 8 channel power relay. The module operates at 5V.
  LCM1602 IIC: I2C-Module to use a 1602 or 2004 LCD on with the wire.h libory Serial LCD Modul
  4x4 Keypad: Matrix membrane keypad 4x4
  MCP23017 IO Expander: Input/Output expander
  DHT11 Humitidy and Temperature Sensor: DHT11 Humidity and Temperature Sensor
  TRANSFORMER VB 1,5/1/9: VB 1,5/1/9 Short circuit proof PCB transformer
